// Logisim project practica03.circ as structural Verilog: 4 circuits, main circuit transistores
module transistores (
  input  AND_gate,
  input  in_2,
  input  OR_gate,
  input  in_4,
  output out_5,
  output out_6
);

  wire transistor_1_out;

  Transistor #(.\type ("n")) transistor_1 (.in(1'b1), .out(transistor_1_out), .gate(AND_gate));
  Transistor #(.\type ("n")) transistor_2 (.in(1'b1), .out(out_6), .gate(OR_gate));
  Transistor #(.\type ("n")) transistor_3 (.in(1'b1), .out(out_6), .gate(in_4));
  Transistor #(.\type ("n")) transistor_4 (.in(transistor_1_out), .out(out_5), .gate(in_2));
endmodule

module bicondicional (
  input  in_1,
  input  in_2,
  output out_3
);

  wire and_1_out, and_2_out, not_1_out, not_2_out;

  not not_1 (not_1_out, in_1);
  not not_2 (not_2_out, in_2);
  and and_1 (and_1_out, in_2, in_1);
  and and_2 (and_2_out, not_1_out, not_2_out);
  or or_1 (out_3, and_1_out, and_2_out);

  // Notes on the sheet:
  //   Bicondicional
endmodule

module comparador1 (
  input  [1:0] X,
  input  [1:0] Y,
  output out_3
);

  wire not_1_out, not_2_out, or_1_out, or_2_out, or_3_out;

  not not_1 (not_1_out, Y[0]);
  not not_2 (not_2_out, Y[1]);
  or or_1 (or_1_out, X[0], X[1], not_1_out);
  or or_2 (or_2_out, X[1], not_2_out);
  or or_3 (or_3_out, not_1_out, X[0], not_2_out);
  and and_1 (out_3, or_1_out, or_2_out, or_3_out);

  // Notes on the sheet:
  //   Comparador x >= y
endmodule

module comparador2 (
  input  [1:0] in_1,
  input  [1:0] y,
  output x_y,
  output x_y_2,
  output x_y_3
);

  wire and_1_out, and_2_out, and_3_out, not_1_out, not_2_out, not_3_out, not_4_out, not_5_out, not_6_out,
       or_1_out, or_2_out, or_3_out, or_4_out;

  not not_1 (not_1_out, in_1[0]);
  not not_2 (not_2_out, in_1[1]);
  not not_3 (not_3_out, y[0]);
  not not_4 (not_4_out, y[1]);
  or or_1 (or_1_out, in_1[0], not_3_out);
  or or_2 (or_2_out, in_1[1], not_4_out);
  or or_3 (or_3_out, not_1_out, y[0]);
  or or_4 (or_4_out, not_2_out, y[1]);
  and and_1 (and_1_out, not_2_out, y[1]);
  and and_2 (and_2_out, not_1_out, not_2_out, y[0]);
  and and_3 (and_3_out, not_1_out, y[1], y[0]);
  and and_4 (x_y, or_1_out, or_2_out, or_3_out, or_4_out);
  or or_5 (x_y_3, and_1_out, and_2_out, and_3_out);
  not not_5 (not_5_out, x_y);
  not not_6 (not_6_out, x_y_3);
  and and_5 (x_y_2, not_5_out, not_6_out);

  // Notes on the sheet:
  //   x
endmodule
