// Logisim project practica04.circ as structural Verilog: 4 circuits, main circuit sumador-c-1bit
module sumador_c_1bit (
  input  A,
  input  B,
  input  Ci,
  output Sum,
  output Co
);

  wire and_1_out, and_2_out, xor_1_out;

  xor xor_1 (xor_1_out, A, B);
  and and_1 (and_1_out, A, B);
  xor xor_2 (Sum, Ci, xor_1_out);
  and and_2 (and_2_out, xor_1_out, Ci);
  or or_1 (Co, and_2_out, and_1_out);

  // Notes on the sheet:
  //   Sumador completo 1-bit
endmodule

module sumador_c_8bits (
  input  [7:0] A,
  input  cin,
  input  [7:0] B,
  output [7:0] Sum,
  output cout
);

  wire sumador_c_1bit_1_co, sumador_c_1bit_2_co, sumador_c_1bit_3_co, sumador_c_1bit_4_co,
       sumador_c_1bit_5_co, sumador_c_1bit_6_co, sumador_c_1bit_7_co;

  sumador_c_1bit sumador_c_1bit_1 (.A(A[0]), .B(B[0]), .Ci(cin), .Sum(Sum[0]), .Co(sumador_c_1bit_1_co));
  sumador_c_1bit sumador_c_1bit_2 (
    .A(A[1]), .B(B[1]), .Ci(sumador_c_1bit_1_co), .Sum(Sum[1]), .Co(sumador_c_1bit_2_co));
  sumador_c_1bit sumador_c_1bit_3 (
    .A(A[2]), .B(B[2]), .Ci(sumador_c_1bit_2_co), .Sum(Sum[2]), .Co(sumador_c_1bit_3_co));
  sumador_c_1bit sumador_c_1bit_4 (
    .A(A[3]), .B(B[3]), .Ci(sumador_c_1bit_3_co), .Sum(Sum[3]), .Co(sumador_c_1bit_4_co));
  sumador_c_1bit sumador_c_1bit_5 (
    .A(A[4]), .B(B[4]), .Ci(sumador_c_1bit_4_co), .Sum(Sum[4]), .Co(sumador_c_1bit_5_co));
  sumador_c_1bit sumador_c_1bit_6 (
    .A(A[5]), .B(B[5]), .Ci(sumador_c_1bit_5_co), .Sum(Sum[5]), .Co(sumador_c_1bit_6_co));
  sumador_c_1bit sumador_c_1bit_7 (
    .A(A[6]), .B(B[6]), .Ci(sumador_c_1bit_6_co), .Sum(Sum[6]), .Co(sumador_c_1bit_7_co));
  sumador_c_1bit sumador_c_1bit_8 (.A(A[7]), .B(B[7]), .Ci(sumador_c_1bit_7_co), .Sum(Sum[7]), .Co(cout));
endmodule

module sum_res_8bits (
  input  cin,
  input  Rin,
  input  [7:0] A,
  input  [7:0] B,
  input  Operation,
  output [7:0] out_6,
  output Cout,
  output Rout
);

  wire [7:0] multiplexer_1_out, not_1_out, sumador_c_8bits_1_sum;

  sumador_c_8bits sumador_c_8bits_1 (.A(not_1_out), .B(8'h1), .Sum(sumador_c_8bits_1_sum), .cout(Rout), .cin(Rin));
  assign not_1_out = ~B;  // NOT_Gate not_1, 8 bits wide
  Multiplexer #(.width(8), .enable("false")) multiplexer_1 (
    .in0(B), .in1(sumador_c_8bits_1_sum), .out(multiplexer_1_out), .sel(Operation));
  sumador_c_8bits sumador_c_8bits_2 (.A(A), .B(multiplexer_1_out), .Sum(out_6), .cout(Cout), .cin(cin));
endmodule

module _16bit_add_sub (
  input  Op,
  input  [15:0] in_2,
  input  [15:0] in_3,
  output [15:0] out_4
);

  wire not_1_out, sum_res_8bits_1_cout, sum_res_8bits_1_rout;

  sum_res_8bits sum_res_8bits_1 (
    .A(in_2[7:0]), .B(in_3[7:0]), .out_6(out_4[7:0]), .Cout(sum_res_8bits_1_cout), .cin(1'b0),
    .Operation(Op), .Rin(1'b0), .Rout(sum_res_8bits_1_rout));
  not not_1 (not_1_out, sum_res_8bits_1_rout);
  sum_res_8bits sum_res_8bits_2 (
    .A(in_2[15:8]), .B(in_3[15:8]), .out_6(out_4[15:8]), .cin(sum_res_8bits_1_cout), .Operation(Op),
    .Rin(not_1_out));  // open: Cout, Rout

  // Notes on the sheet:
  //   Sumador de 16 bits
endmodule
